// Logisim project control_logic.circ as structural Verilog: 1 circuit, main circuit control_logic
module control_logic (
  input  [31:0] inst,
  input  BrEq,
  input  BrLt,
  output PCSel,
  output RegWEn,
  output [2:0] ImmSel,
  output BrUn,
  output ASel,
  output BSel,
  output [3:0] ALUSel,
  output MemRW,
  output [1:0] WBSel,
  output CSRSel,
  output CSRWen
);

  wire comparator_1_eq, comparator_2_eq, comparator_3_eq, comparator_4_eq, comparator_5_eq, comparator_6_eq,
       comparator_7_eq, comparator_8_eq, comparator_9_eq, comparator_10_eq, comparator_11_eq,
       comparator_12_eq, comparator_13_eq, isIorR, isMul, isMulh, isSra, isSub;
  wire [3:0] multiplexer_1_out, multiplexer_2_out, multiplexer_3_out, multiplexer_4_out, multiplexer_5_out;

  Multiplexer #(.enable("false"), .select(3), .width(4)) multiplexer_1 (
    .in0(4'b0000), .in1(4'b0110), .in2(4'b0111), .in3(4'b1011), .in4(4'b0011), .in5(4'b0100), .in6(4'b0010),
    .in7(4'b0001), .out(multiplexer_1_out), .sel(inst[14:12]));
  Comparator #(.width(7)) comparator_1 (.a(inst[31:25]), .b(7'b0000001), .eq(comparator_1_eq));  // open: gt, lt
  Comparator #(.width(3)) comparator_2 (.a(inst[14:12]), .b(3'b000), .eq(comparator_2_eq));  // open: gt, lt
  Comparator #(.width(7)) comparator_3 (.a(inst[6:0]), .b(7'b0110011), .eq(comparator_3_eq));  // open: gt, lt
  Comparator #(.width(7)) comparator_4 (.a(inst[31:25]), .b(7'b0000001), .eq(comparator_4_eq));  // open: gt, lt
  Comparator #(.width(3)) comparator_5 (.a(inst[14:12]), .b(3'b001), .eq(comparator_5_eq));  // open: gt, lt
  Comparator #(.width(7)) comparator_6 (.a(inst[6:0]), .b(7'b0110011), .eq(comparator_6_eq));  // open: gt, lt
  Multiplexer #(.enable("false"), .width(4)) multiplexer_2 (
    .in0(multiplexer_1_out), .in1(4'b1010), .out(multiplexer_2_out), .sel(isMul));
  and and_1 (isMul, comparator_1_eq, comparator_2_eq, comparator_3_eq);
  and and_2 (isMulh, comparator_4_eq, comparator_5_eq, comparator_6_eq);
  Multiplexer #(.enable("false"), .width(4)) multiplexer_3 (
    .in0(multiplexer_2_out), .in1(4'b1011), .out(multiplexer_3_out), .sel(isMulh));
  Multiplexer #(.enable("false"), .width(4)) multiplexer_4 (
    .in0(multiplexer_3_out), .in1(4'b1100), .out(multiplexer_4_out), .sel(isSub));
  Multiplexer #(.enable("false"), .width(4)) multiplexer_5 (
    .in0(multiplexer_4_out), .in1(4'b1100), .out(multiplexer_5_out), .sel(isSra));
  Comparator #(.width(7)) comparator_7 (.a(inst[31:25]), .b(7'b0100000), .eq(comparator_7_eq));  // open: gt, lt
  Comparator #(.width(3)) comparator_8 (.a(inst[14:12]), .b(3'b000), .eq(comparator_8_eq));  // open: gt, lt
  Comparator #(.width(7)) comparator_9 (.a(inst[6:0]), .b(7'b0110011), .eq(comparator_9_eq));  // open: gt, lt
  Comparator #(.width(7)) comparator_10 (.a(inst[31:25]), .b(7'b0100000), .eq(comparator_10_eq));  // open: gt, lt
  Comparator #(.width(3)) comparator_11 (.a(inst[14:12]), .b(3'b101), .eq(comparator_11_eq));  // open: gt, lt
  Multiplexer #(.enable("false"), .width(4)) multiplexer_6 (
    .in0(4'b0000), .in1(multiplexer_5_out), .out(ALUSel), .sel(isIorR));
  and and_3 (isSub, comparator_7_eq, comparator_8_eq, comparator_9_eq);
  and and_4 (isSra, comparator_10_eq, comparator_11_eq);
  Comparator #(.width(7)) comparator_12 (.a(inst[6:0]), .b(7'b0110011), .eq(comparator_12_eq));  // open: gt, lt
  Comparator #(.width(7)) comparator_13 (.a(inst[6:0]), .b(7'b0010011), .eq(comparator_13_eq));  // open: gt, lt
  or or_1 (isIorR, comparator_12_eq, comparator_13_eq);

  assign RegWEn = 1'b1;

  // Other names for the same wires on the sheet: op[6:0] = inst[6:0]; rd[4:0] = inst[11:7]; funct3[2:0] = inst[14:12];
  //   rs1[4:0] = inst[19:15]; rs2[4:0] = inst[24:20]; funct7[6:0] = inst[31:25]

  // Notes on the sheet:
  //   INPUTS to your circuit
  //   decode
  //   ALU select
  //   DON'T CHANGE THE LOCATIONS OF THE INPUTS AND OUTPUTS!
  //   OUTPUT from your circuit
endmodule
